// Logisim project MIPS 4-bit CPU.circ as structural Verilog: 1 circuit, main circuit 4-bit CPU
module _4_bit_CPU (
);

  wire and_1_out, Clk_out, controlsignal_1_p2, controlsignal_1_p3, controlsignal_1_p4, controlsignal_1_p5,
       controlsignal_1_p6, controlsignal_1_p7, controlsignal_1_p8, controlsignal_1_p9, controlsignal_1_p10,
       instruction_1_p8, mips_alu_4_bit_1_p4;
  wire [3:0] adder_1_p3, adder_2_p3, instruction_1_p5, instruction_1_p6, instruction_1_p7,
       mips_alu_4_bit_1_p5, multiplexer_1_out, multiplexer_2_out, multiplexer_3_out, multiplexer_4_out,
       multiplexer_5_out, PC_q, ram_1_data, registerfile_1_r1_data, registerfile_1_r2_data;

  Register #(.width(4)) PC (.D(multiplexer_1_out), .Q(PC_q), .clk(Clk_out));  // open: en, clr
  Clock Clk (.out(Clk_out));
  // Adder adder_1: pin names not known; wires that end beside it: 4'b0001, PC_q, adder_1_p3
  // instruction instruction_1: pin names not known; wires that end beside it: PC_q, 1'b0, 1'b1, Clk_out, instruction_1_p5, instruction_1_p6, instruction_1_p7, instruction_1_p8
  Multiplexer #(.width(4), .disabled(0), .enable("false")) multiplexer_1 (
    .in0(multiplexer_3_out), .in1(instruction_1_p7), .out(multiplexer_1_out), .sel(controlsignal_1_p7));
  // Adder adder_2: pin names not known; wires that end beside it: adder_1_p3, instruction_1_p7, adder_2_p3
  // ControlSignal controlsignal_1: pin names not known; wires that end beside it: instruction_1_p8, controlsignal_1_p2, controlsignal_1_p3, controlsignal_1_p4, controlsignal_1_p5, controlsignal_1_p6, controlsignal_1_p7, controlsignal_1_p8, controlsignal_1_p9, controlsignal_1_p10
  and and_1 (and_1_out, mips_alu_4_bit_1_p4, controlsignal_1_p5);
  Multiplexer #(.width(4), .disabled(0), .enable("false")) multiplexer_2 (
    .in0(instruction_1_p6), .in1(instruction_1_p7), .out(multiplexer_2_out), .sel(controlsignal_1_p10));
  Multiplexer #(.width(4), .disabled(0), .enable("false")) multiplexer_3 (
    .in0(adder_1_p3), .in1(adder_2_p3), .out(multiplexer_3_out), .sel(and_1_out));
  RegisterFile registerfile_1 (
    .Write_Data(multiplexer_5_out), .RegWrite(controlsignal_1_p9), .Write_num(multiplexer_2_out),
    .R1_Data(registerfile_1_r1_data), .R2_Data(registerfile_1_r2_data), .R1_num(instruction_1_p5),
    .R2_num(instruction_1_p6), .Clk(Clk_out));
  Multiplexer #(.width(4), .disabled(0), .enable("false")) multiplexer_4 (
    .in0(registerfile_1_r2_data), .in1(instruction_1_p7), .out(multiplexer_4_out), .sel(controlsignal_1_p2));
  // MIPS_ALU_4_bit mips_alu_4_bit_1: pin names not known; wires that end beside it: registerfile_1_r1_data, multiplexer_4_out, controlsignal_1_p4, mips_alu_4_bit_1_p4, mips_alu_4_bit_1_p5
  RAM #(.addrWidth(4), .dataWidth(4), .bus("separate")) ram_1 (
    .addr(mips_alu_4_bit_1_p5), .din(registerfile_1_r2_data), .data(ram_1_data), .str(controlsignal_1_p6),
    .clk(Clk_out), .ld(controlsignal_1_p8));  // open: sel, clr
  Multiplexer #(.width(4), .disabled(0), .enable("false")) multiplexer_5 (
    .in0(mips_alu_4_bit_1_p5), .in1(ram_1_data), .out(multiplexer_5_out), .sel(controlsignal_1_p3));

  // Notes on the sheet:
  //   PCSrc.J
  //   writeDest
  //       PCSrc.beq
  //             RegWriteEN
  //        ALUSrc
  //   ALUOp
  //          MemWrite
  //   MemRead
  //         w.val.src
endmodule
