// Logisim project RegFile.circ as structural Verilog: 2 circuits, main circuit main
module main (
  input  [3:0] writeData,
  input  [3:0] r1_num,
  input  [3:0] r2_num,
  input  [3:0] w_num,
  input  RegWriteEN,
  output [3:0] r1_data,
  output [3:0] r2_data
);

  wire clock_1_out;

  Clock clock_1 (.out(clock_1_out));
  RegisterFile registerfile_1 (
    .Write_Data(writeData), .RegWrite(RegWriteEN), .Write_num(w_num), .R1_Data(r1_data), .R2_Data(r2_data),
    .R1_num(r1_num), .R2_num(r2_num), .Clk(clock_1_out));
endmodule

module RegisterFile (
  input  [3:0] R1_num,
  input  [3:0] R2_num,
  input  [3:0] Write_Data,
  input  RegWrite,
  input  Clk,
  input  [3:0] Write_num,
  output [3:0] R1_Data,
  output [3:0] R2_Data
);

  wire and_1_out, demultiplexer_1_out0, demultiplexer_1_out1, demultiplexer_1_out2, demultiplexer_1_out3,
       demultiplexer_1_out4, demultiplexer_1_out5, demultiplexer_1_out6, demultiplexer_1_out7, not_1_out;
  wire [3:0] _0__zero_q, _1_q, _2_q, _3_q, _4_q, _5_q, _6_q, _7__sp_q;

  not not_1 (not_1_out, Clk);
  and and_1 (and_1_out, RegWrite, not_1_out);
  Demultiplexer #(.select(3), .disabled(0), .enable("false")) demultiplexer_1 (
    .out0(demultiplexer_1_out0), .out1(demultiplexer_1_out1), .out2(demultiplexer_1_out2),
    .out3(demultiplexer_1_out3), .out4(demultiplexer_1_out4), .out5(demultiplexer_1_out5),
    .out6(demultiplexer_1_out6), .out7(demultiplexer_1_out7), .in(and_1_out), .sel(Write_num[2:0]));
  Register #(.width(4)) _0__zero (.D(4'b0000), .Q(_0__zero_q), .clk(demultiplexer_1_out0));  // open: en, clr
  Register #(.width(4)) _1 (.D(Write_Data), .Q(_1_q), .clk(demultiplexer_1_out1));  // open: en, clr
  Register #(.width(4)) _2 (.D(Write_Data), .Q(_2_q), .clk(demultiplexer_1_out2));  // open: en, clr
  Register #(.width(4)) _3 (.D(Write_Data), .Q(_3_q), .clk(demultiplexer_1_out3));  // open: en, clr
  Register #(.width(4)) _4 (.D(Write_Data), .Q(_4_q), .clk(demultiplexer_1_out4));  // open: en, clr
  Register #(.width(4)) _5 (.D(Write_Data), .Q(_5_q), .clk(demultiplexer_1_out5));  // open: en, clr
  Register #(.width(4)) _6 (.D(Write_Data), .Q(_6_q), .clk(demultiplexer_1_out6));  // open: en, clr
  Register #(.width(4)) _7__sp (.D(Write_Data), .Q(_7__sp_q), .clk(demultiplexer_1_out7));  // open: en, clr
  Multiplexer #(.select(3), .width(4), .disabled(0), .enable("false")) multiplexer_1 (
    .in0(_0__zero_q), .in1(_1_q), .in2(_2_q), .in3(_3_q), .in4(_4_q), .in5(_5_q), .in6(_6_q), .in7(_7__sp_q),
    .out(R1_Data), .sel(R1_num[2:0]));
  Multiplexer #(.select(3), .width(4), .disabled(0), .enable("false")) multiplexer_2 (
    .in0(_0__zero_q), .in1(_1_q), .in2(_2_q), .in3(_3_q), .in4(_4_q), .in5(_5_q), .in6(_6_q), .in7(_7__sp_q),
    .out(R2_Data), .sel(R2_num[2:0]));
endmodule
