// Logisim project MIPS 4-bit CPU.circ as structural Verilog: 1 circuit, main circuit 4-bit CPU
module _4_bit_CPU (
);

  wire mips_alu_4_bit_1_p3, undriven_4, undriven_5, undriven_6, undriven_7, undriven_8, undriven_9;
  wire [3:0] mips_alu_4_bit_1_p4, multiplexer_1_out, multiplexer_2_out, multiplexer_3_out, ram_1_data,
       registerfile_1_r1_data, registerfile_1_r2_data, undriven, undriven_2, undriven_3;

  Clock Clk ();  // open: out
  Multiplexer #(.width(4), .disabled(0), .enable("false")) multiplexer_1 (
    .in0(undriven_2), .in1(undriven_3), .out(multiplexer_1_out), .sel(undriven_4));
  RegisterFile registerfile_1 (
    .Write_Data(multiplexer_3_out), .RegWrite(undriven_5), .Write_num(multiplexer_1_out),
    .R1_Data(registerfile_1_r1_data), .R2_Data(registerfile_1_r2_data), .R1_num(undriven), .R2_num(undriven_2));  // open: Clk
  Multiplexer #(.width(4), .disabled(0), .enable("false")) multiplexer_2 (
    .in0(registerfile_1_r2_data), .in1(undriven_3), .out(multiplexer_2_out), .sel(undriven_6));
  // MIPS_ALU_4_bit mips_alu_4_bit_1: pin names not known; wires that end beside it: registerfile_1_r1_data, multiplexer_2_out, mips_alu_4_bit_1_p3, mips_alu_4_bit_1_p4
  RAM #(.addrWidth(4), .dataWidth(4), .bus("separate")) ram_1 (
    .addr(mips_alu_4_bit_1_p4), .din(registerfile_1_r2_data), .data(ram_1_data), .str(undriven_7),
    .ld(undriven_8));  // open: sel, clk, clr
  Multiplexer #(.width(4), .disabled(0), .enable("false")) multiplexer_3 (
    .in0(mips_alu_4_bit_1_p4), .in1(ram_1_data), .out(multiplexer_3_out), .sel(undriven_9));

  // Notes on the sheet:
  //   writeDest
  //             RegWriteEN
  //        ALUSrc
  //   ALUOp
  //          MemWrite
  //   MemRead
  //         w.val.src
endmodule
