// Logisim project RegFile.circ as structural Verilog
module RegisterFile (
  input  [3:0] WriteData,
  input  RegWrite,
  input  [2:0] Write_num
);

  wire demultiplexer_1_out0, demultiplexer_1_out1, demultiplexer_1_out2, demultiplexer_1_out3,
       demultiplexer_1_out4, demultiplexer_1_out5, demultiplexer_1_out6, demultiplexer_1_out7;
  wire [3:0] _000_q, _001_q, _002_q, _003_q, _004_q, _005_q, _006_q, _007_q, multiplexer_1_out,
       multiplexer_2_out;

  Demultiplexer #(.select(3), .disabled(0), .enable("false")) demultiplexer_1 (
    .out0(demultiplexer_1_out0), .out1(demultiplexer_1_out1), .out2(demultiplexer_1_out2),
    .out3(demultiplexer_1_out3), .out4(demultiplexer_1_out4), .out5(demultiplexer_1_out5),
    .out6(demultiplexer_1_out6), .out7(demultiplexer_1_out7), .in(RegWrite), .sel(Write_num));
  Register #(.width(4)) _000 (.D(WriteData), .Q(_000_q), .clk(demultiplexer_1_out0));  // open: en, clr
  Register #(.width(4)) _001 (.D(WriteData), .Q(_001_q), .clk(demultiplexer_1_out1));  // open: en, clr
  Register #(.width(4)) _002 (.D(WriteData), .Q(_002_q), .clk(demultiplexer_1_out2));  // open: en, clr
  Register #(.width(4)) _003 (.D(WriteData), .Q(_003_q), .clk(demultiplexer_1_out3));  // open: en, clr
  Register #(.width(4)) _004 (.D(WriteData), .Q(_004_q), .clk(demultiplexer_1_out4));  // open: en, clr
  Register #(.width(4)) _005 (.D(WriteData), .Q(_005_q), .clk(demultiplexer_1_out5));  // open: en, clr
  Register #(.width(4)) _006 (.D(WriteData), .Q(_006_q), .clk(demultiplexer_1_out6));  // open: en, clr
  Register #(.width(4)) _007 (.D(WriteData), .Q(_007_q), .clk(demultiplexer_1_out7));  // open: en, clr
  Multiplexer #(.select(3), .width(4), .disabled(0), .enable("false")) multiplexer_1 (
    .in0(_000_q), .in1(_001_q), .in2(_002_q), .in3(_003_q), .in4(_004_q), .in5(_005_q), .in6(_006_q),
    .in7(_007_q), .out(multiplexer_1_out));  // open: sel
  Multiplexer #(.select(3), .width(4), .disabled(0), .enable("false")) multiplexer_2 (
    .in0(_000_q), .in1(_001_q), .in2(_002_q), .in3(_003_q), .in4(_004_q), .in5(_005_q), .in6(_006_q),
    .in7(_007_q), .out(multiplexer_2_out));  // open: sel
  // Transmission_Gate #(.width(4)) transmission_1: pin names not known; wires that end beside it: multiplexer_1_out
  // Transmission_Gate #(.width(4)) transmission_2: pin names not known; wires that end beside it: WriteData, multiplexer_2_out
endmodule
